// Logisim project comp.circ as structural Verilog: 2 circuits, main circuit main
module main (
  input  [3:0] in_1,
  input  in_2,
  input  [3:0] in_3,
  input  [3:0] in_4,
  input  in_5,
  output [7:0] out_6,
  output [7:0] out_7,
  output [3:0] out_8
);

  wire A_In, A_Out, Alu_Mode_1, Alu_Mode_2, Alu_Out, B_In, B_Out, button_1_out, clock_1_out, clock_2_out,
       clock_3_out, clock_4_out, clock_5_out, clock_6_out, clock_7_out, clock_8_out, Count_En, Count_Jump,
       Count_Out, decoder_1_out5, HLT, Instruction_In, Instruction_Out, multiplexer_3_out, not_1_out,
       or_1_out, or_2_out, Output_In, Ram_Adr_In, Ram_Data_In, Ram_Data_Out, RST;
  wire [2:0] counter_2_q;
  wire [3:0] Instructions, multiplexer_1_out, register_2_q, register_4_q;
  wire [7:0] A, adder_1_out, and_1_out, B, multiplexer_2_out, multiplexer_4_out, or_3_out, ram_1_dout,
       subtractor_1_out;

  Clock clock_1 (.out(clock_1_out));
  Clock clock_2 (.out(clock_2_out));
  Register register_1 (.D(out_7), .en(A_In), .clk(clock_1_out), .Q(A), .clr(RST));
  not not_1 (not_1_out, clock_2_out);
  assign out_7 = A_Out ? A : 8'bz;  // Controlled_Buffer controlled_buffer_1
  Counter #(.max('hf), .width(4)) counter_1 (
    .load(Count_Jump), .D(out_7[3:0]), .count(Count_En), .Q(out_8), .clk(clock_3_out), .clr(RST));  // open: carry, up
  Clock clock_3 (.out(clock_3_out));
  Register #(.width(4)) register_2 (.D(out_7[3:0]), .en(Ram_Adr_In), .clk(clock_4_out), .Q(register_2_q), .clr(RST));
  Clock clock_4 (.out(clock_4_out));
  Counter #(.max('h7), .width(3)) counter_2 (
    .Q(counter_2_q), .clk(not_1_out), .clr(or_1_out));  // open: load, D, count, carry, up
  or or_1 (or_1_out, RST, decoder_1_out5);
  Decoder #(.select(3)) decoder_1 (
    .out5(decoder_1_out5), .sel(counter_2_q));  // open: out0, out1, out2, out3, out4, out6, out7, en
  ROM #(.addrWidth(7), .dataWidth(16)) rom_1 (
    .addr({Instructions, counter_2_q}),
    .data({A_In, A_Out, B_In, Alu_Mode_1, Alu_Mode_2, Alu_Out, Count_En, Count_Out, Count_Jump, Instruction_In, Instruction_Out, Ram_Adr_In, Ram_Data_In, Ram_Data_Out, Output_In, HLT}));
  assign out_7 = Count_Out ? {4'b0000, out_8} : 8'bz;  // Controlled_Buffer controlled_buffer_2
  Multiplexer #(.width(4)) multiplexer_1 (.in0(in_1), .in1(register_2_q), .out(multiplexer_1_out), .sel(in_2));
  Multiplexer #(.width(8)) multiplexer_2 (.in0({in_3, in_4}), .in1(out_7), .out(multiplexer_2_out), .sel(in_2));
  Register register_3 (.D(out_7), .en(B_In), .clk(clock_5_out), .Q(B), .clr(RST));
  Clock clock_5 (.out(clock_5_out));
  Clock clock_6 (.out(clock_6_out));
  or or_2 (or_2_out, clock_6_out, button_1_out);
  Button button_1 (.out(button_1_out));
  RAM #(.addrWidth(4), .asyncread("true")) ram_1 (
    .addr(multiplexer_1_out), .we(multiplexer_3_out), .clk(or_2_out), .din(multiplexer_2_out),
    .dout(ram_1_dout));  // open: oe
  Multiplexer multiplexer_3 (.in0(in_5), .in1(Ram_Data_In), .out(multiplexer_3_out), .sel(in_2));
  assign out_7 = B_Out ? B : 8'bz;  // Controlled_Buffer controlled_buffer_3
  Adder adder_1 (.a(A), .b(B), .out(adder_1_out));  // open: cin, cout
  Subtractor subtractor_1 (.a(A), .b(B), .out(subtractor_1_out));  // open: bin, bout
  assign and_1_out = A & B;  // AND_Gate and_1, 8 bits wide
  assign or_3_out = A | B;  // OR_Gate or_3, 8 bits wide
  assign out_7 = Alu_Out ? multiplexer_4_out : 8'bz;  // Controlled_Buffer controlled_buffer_4
  Multiplexer #(.select(2), .width(8)) multiplexer_4 (
    .in0(adder_1_out), .in1(subtractor_1_out), .in2(and_1_out), .in3(or_3_out), .out(multiplexer_4_out),
    .sel({Alu_Mode_2, Alu_Mode_1}));
  assign out_7 = Ram_Data_Out ? ram_1_dout : 8'bz;  // Controlled_Buffer controlled_buffer_5
  Register register_4 (.D(out_7), .en(Instruction_In), .clk(clock_7_out), .Q({Instructions, register_4_q}), .clr(RST));
  Clock clock_7 (.out(clock_7_out));
  assign out_7 = Instruction_Out ? {4'b0000, register_4_q} : 8'bz;  // Controlled_Buffer controlled_buffer_6
  Register register_5 (.D(out_7), .en(Output_In), .clk(clock_8_out), .Q(out_6), .clr(RST));
  Clock clock_8 (.out(clock_8_out));
  Button button_2 (.out(RST));
  LED led_1 (.in(HLT));
  Clock clock_9 ();  // open: out

  // Other names for the same wires on the sheet: B_U_S[7:0] = out_7; Count[3:0] = out_8; ANS[7:0] = out_6

  // Notes on the sheet:
  //   A Register
  //   Counter
  //   contents of rom_1 (hex, n*v repeats v):
  //   110 244 6*0 110 244 30 8004 4*0 110 244 30 2004 8400 0 0 0 110 244 30 2004 9400 0 0 0 110 244 30
  //   2004 8c00 0 0 0 110 244 30 2004 9c00 0 0 0 110 244 30 4008 4*0 110 244 8020 5*0 110 244 a0 5*0 110
  //   244 6*0 110 244 6*0 110 244 6*0 110 244 6*0 110 244 6*0 110 244 4002 5*0 110 244 1
  //   RAM
  //   B Register
  //   Control Logic
  //   ALU
  //   Instruction Register
  //   Output Register
endmodule

module G (
  input  [3:0] in_1,
  input  [2:0] in_2,
  input  in_3,
  input  [7:0] in_4,
  input  [7:0] in_5,
  input  [3:0] in_6,
  input  [3:0] in_7,
  input  [3:0] in_8,
  output [7:0] out_9
);

  wire button_1_out, clock_1_out, I_1, I_2, I_3, I_4, I_5, I_6, I_7, I_8, I_9, I_10, I_11, I_12, I_13, I_14,
       I_15, I_16;

  Button button_1 (.out(button_1_out));
  RAM #(.addrWidth(4), .asyncread("true")) ram_1 (
    .addr(in_6), .we(1'b1), .oe(1'b1), .clk(button_1_out), .din({in_7, in_8}), .dout(out_9));
  RAM #(.addrWidth(7), .asyncread("true"), .dataWidth(16)) ram_2 (
    .addr({in_1, in_2}), .we(in_3), .clk(clock_1_out), .din({in_4, in_5}),
    .dout({I_1, I_2, I_3, I_4, I_5, I_6, I_7, I_8, I_9, I_10, I_11, I_12, I_13, I_14, I_15, I_16}));  // open: oe
  Clock clock_1 (.out(clock_1_out));
endmodule
